// Logisim project control-logic.circ as structural Verilog: 1 circuit, main circuit control_logic
module control_logic (
  input  [31:0] inst,
  input  BrEq,
  input  BrLt,
  output PCSel,
  output RegWEn,
  output [2:0] ImmSel,
  output BrUn,
  output ASel,
  output BSel,
  output [3:0] ALUSel,
  output MemRW,
  output [1:0] WBSel,
  output CSRSel,
  output CSRWen
);

  wire and_28_out, is_addi, is_and, is_andi, is_auipc, is_CSRRWI, is_I_type, is_I_type_0x03, is_I_type_0x67,
       is_I_type_0x73, is_lui, is_mul, is_mulh, is_mulhu, is_or, is_ori, is_SB_or_is_jalr, is_sll, is_slli,
       is_slt, is_slti, is_sra, is_srai, is_srl, is_srli, is_sub, is_U_type, is_xor, is_xori, or_8_out,
       or_10_out;

  and and_1 (is_sll, inst[12], BSel);
  and and_2 (is_mulh, inst[12], inst[25], BSel);
  and and_3 (is_srl, inst[14], inst[12], BSel);
  and and_4 (is_slli, inst[12], is_addi);
  Priority_Encoder priority_encoder_1 (
    .in0(is_I_type), .in1(is_U_type), .in2(MemRW), .in3(is_SB_or_is_jalr), .in4(WBSel[1]), .in5(BSel),
    .out(ImmSel));  // open: in6, in7, en_in, gs, en_out
  and and_5 (is_mulhu, inst[13], inst[14], inst[25], BSel);
  and and_6 (is_sra, inst[14], inst[12], inst[30], BSel);
  and and_7 (is_and, inst[12], inst[13], inst[14], BSel);
  and and_8 (is_srli, inst[14], inst[12], is_addi);
  and and_9 (is_srai, inst[14], inst[12], is_addi, inst[30]);
  and and_10 (is_andi, inst[12], inst[13], inst[14], is_addi);
  and and_11 (is_I_type_0x03, inst[0], inst[1], ~inst[2], ~inst[3], ~inst[4], ~inst[5], ~inst[6]);  // AND_Gate
  and and_12 (is_addi, inst[0], inst[1], ~inst[2], ~inst[3], inst[4], ~inst[5], ~inst[6]);  // AND_Gate
  and and_13 (is_I_type_0x67, inst[0], inst[1], inst[2], ~inst[3], ~inst[4], inst[5], inst[6]);  // AND_Gate
  and and_14 (is_I_type_0x73, inst[0], inst[1], ~inst[2], ~inst[3], inst[4], inst[5], inst[6]);  // AND_Gate
  and and_15 (is_auipc, inst[0], inst[1], inst[2], ~inst[3], inst[4], ~inst[5], ~inst[6]);  // AND_Gate
  and and_16 (is_sub, inst[30], BSel);
  and and_17 (is_xor, inst[14], BSel);
  and and_18 (is_slt, inst[13], BSel);
  and and_19 (is_or, inst[13], inst[14], BSel);
  and and_20 (is_slti, inst[13], is_addi);
  and and_21 (is_ori, inst[13], inst[14], is_addi);
  and and_22 (is_xori, inst[14], is_addi);
  and and_23 (is_mul, inst[25], BSel);
  and and_24 (CSRSel, is_I_type_0x73, inst[12], ~inst[13], ~inst[14]);  // AND_Gate
  or or_1 (WBSel[0], is_slt, is_sub, BSel, is_mul, is_sll, is_mulh, is_mulhu, is_xor, is_srl, is_sra, is_or, is_and, is_addi, is_slli, is_slti, is_xori, is_srli, is_srai, is_ori, is_andi, is_auipc, is_lui);
  and and_25 (is_SB_or_is_jalr, inst[0], inst[1], inst[2], ~inst[3], ~inst[4], inst[5], inst[6]);  // AND_Gate
  and and_26 (WBSel[1], inst[0], inst[1], inst[2], inst[3], ~inst[4], inst[5], inst[6]);  // AND_Gate
  or or_2 (ALUSel[1], is_mulhu, is_slt, is_or, is_and, is_slti, is_ori, is_andi, is_lui);
  or or_3 (ALUSel[2], is_sub, is_xor, is_srl, is_sra, is_or, is_and, is_xori, is_srli, is_srai, is_ori, is_andi, is_lui);
  or or_4 (ALUSel[3], is_mul, is_sub, is_mulh, is_mulhu, is_sra, is_srai, is_lui);
  or or_5 (PCSel, is_SB_or_is_jalr, WBSel[1]);
  or or_6 (is_I_type, is_I_type_0x03, is_addi, is_I_type_0x67, is_I_type_0x73);
  or or_7 (is_U_type, is_lui, is_auipc);
  or or_8 (or_8_out, MemRW, is_SB_or_is_jalr);
  not not_1 (RegWEn, or_8_out);
  and and_27 (is_CSRRWI, is_I_type_0x73, inst[12], ~inst[13], inst[14]);  // AND_Gate
  or or_9 (ALUSel[0], is_sll, is_mulh, is_mulhu, is_srl, is_sra, is_and, is_slli, is_srli, is_srai, is_andi);
  and and_28 (and_28_out, inst[13], inst[14]);
  and and_29 (is_lui, inst[0], inst[1], inst[2], ~inst[3], inst[4], inst[5], ~inst[6]);  // AND_Gate
  and and_30 (is_auipc, inst[0], inst[1], inst[2], ~inst[3], inst[4], ~inst[5], ~inst[6]);  // AND_Gate
  and and_31 (BSel, inst[0], inst[1], ~inst[2], ~inst[3], inst[4], inst[5], ~inst[6]);  // AND_Gate
  and and_32 (MemRW, inst[0], inst[1], ~inst[2], ~inst[3], ~inst[4], inst[5], ~inst[6]);  // AND_Gate
  and and_33 (BrUn, is_SB_or_is_jalr, and_28_out);
  or or_10 (or_10_out, is_SB_or_is_jalr, WBSel[1], is_auipc);
  not not_2 (ASel, or_10_out);

  assign CSRWen = 1'b1;

  // Other names for the same wires on the sheet: alu_xxx1 = ALUSel[0]; alu_xx1x = ALUSel[1]; alu_x1xx = ALUSel[2];
  //   alu_1xxx = ALUSel[3]; opcode[6:0] = inst[6:0]; opcode_0 = inst[0]; opcode_1 = inst[1]; opcode_2 = inst[2];
  //   opcode_3 = inst[3]; opcode_4 = inst[4]; opcode_5 = inst[5]; opcode_6 = inst[6]; rd[4:0] = inst[11:7];
  //   funct3[2:0] = inst[14:12]; funct3_0 = inst[12]; funct3_1 = inst[13]; funct3_2 = inst[14];
  //   rs1[4:0] = inst[19:15]; imm[11:0] = inst[31:20]; rs2[4:0] = inst[24:20]; funct7[6:0] = inst[31:25];
  //   funct7_0 = inst[25]; immed[6:0] = inst[31:25]; funct7_1 = inst[26]; funct7_2 = inst[27]; funct7_3 = inst[28];
  //   funct7_4 = inst[29]; funct7_5 = inst[30]; funct7_6 = inst[31]; is_add = BSel; is_R_type = BSel;
  //   is_I_type_0x13 = is_addi; is_U_type_0x17 = is_auipc; is_CSRRW = CSRSel; is_U_type_0x37 = is_lui;
  //   is_S_type = MemRW; is_SB_type = is_SB_or_is_jalr; WBSel_x1 = WBSel[0]; is_jal = WBSel[1]; is_UJ_type = WBSel[1];
  //   WBSel_1x = WBSel[1]

  // Notes on the sheet:
  //   I-type: 000,0011
  //   U-type: 001,0111
  //   S-type: 010,0011
  //   R-type: 011,0011; no imm
  //   SB-type: 110,0011
  //   UJ-type: 110,1111
  //   INPUTS to your circuit
  //   ImmSel generator logic
  //   while writting ImmSel, Rtype does not contain imm, so Rtype would not be included.
  //   there is another way to design this circuit, refer to cnblogs: 16225150 
  //   DON'T CHANGE THE LOCATIONS OF THE INPUTS AND OUTPUTS!
  //   OUTPUT from your circuit
  //   the rightest 2 bit always be 1 in these instruction, so this 2 bit would not be contained. becasue this 2 bit cannot identify instrcut type
  //   the highest(leftest) bits shows a regularity. Itype-> 000, Utype->001, Stype->010, SBType-> 110, UJType->110
  //   these 3bits cannot distinct UJ/SB type only, but the 3rd bit is 1 only in UJType. so we can make OR between highest 3bits and extended 3rd bit, to produce a regularity 3bits
  //   THIS CONTROL LOGIC CONTAINS HARD-WIRTED CIRCUIT(ONLY PART OF INSTRUCTIONS WORKS), BECAUSE THIS PROJECT TEST FEW OF INSTRUCTIOS ONLY
  //   PCSel
  //   BrUn
endmodule
