// Logisim project cpu.circ as structural Verilog: 1 circuit, main circuit cpu
module cpu (
  input  clk,
  input  [31:0] INSTRUCTION,
  input  [31:0] READ_DATA,
  output [31:0] WRITE_ADDRESS,
  output [31:0] PROGRAM_COUNTER,
  output [31:0] ra,
  output [31:0] sp,
  output [31:0] t0,
  output [31:0] t1,
  output [31:0] t2,
  output [31:0] s0,
  output [31:0] s1,
  output [31:0] a0,
  output [31:0] tohost,
  output [3:0] WRITE_ENABLE,
  output [31:0] WRITE_DATA
);

  wire ASel, breq, brlt, brun, BSel, CSRSel, CSRWen, MemRW, PCSel, RegWEn;
  wire [1:0] WBSel;
  wire [2:0] control_logic_1_immsel;
  wire [3:0] ALUSel;
  wire [31:0] bit_extender_1_out, CSR_din, imm, multiplexer_1_out, multiplexer_2_out, multiplexer_3_out,
       pcplus4, rs1_data, WB;

  Adder #(.width(32)) adder_1 (.a(PROGRAM_COUNTER), .b(32'h4), .out(pcplus4));  // open: cin, cout
  Multiplexer #(.width(32)) multiplexer_1 (.in0(pcplus4), .in1(WRITE_ADDRESS), .out(multiplexer_1_out), .sel(PCSel));
  Register #(.width(32)) PC (.D(multiplexer_1_out), .en(1'b1), .clk(clk), .Q(PROGRAM_COUNTER));  // open: clr
  branch_comp branch_comp_1 (.rs1(rs1_data), .rs2(WRITE_DATA), .BrUn(brun), .BrEq(breq), .BrLt(brlt));
  // Probe on PCSel
  // Probe on imm
  imm_gen imm_gen_1 (.inst(INSTRUCTION), .ImmSel(control_logic_1_immsel), .imm(imm));
  // Probe on RegWEn
  control_logic control_logic_1 (
    .inst(INSTRUCTION), .BrEq(breq), .BrLt(brlt), .CSRWen(CSRWen), .PCSel(PCSel), .RegWEn(RegWEn),
    .ImmSel(control_logic_1_immsel), .BrUn(brun), .ASel(ASel), .BSel(BSel), .ALUSel(ALUSel), .MemRW(MemRW),
    .WBSel(WBSel), .CSRSel(CSRSel));
  // Probe on breq
  // Probe on control_logic_1_immsel
  regfile regfile_1 (
    .rs1(INSTRUCTION[19:15]), .rs2(INSTRUCTION[24:20]), .rd(INSTRUCTION[11:7]), .Write_Data(WB),
    .RegWEn(RegWEn), .clk(clk), .ra(ra), .sp(sp), .t0(t0), .t1(t1), .t2(t2), .s0(s0), .s1(s1), .a0(a0),
    .Read_Data_1(rs1_data), .Read_Data_2(WRITE_DATA));
  // Probe on ASel
  // Probe on brun
  // Probe on BSel
  // Probe on ALUSel
  Multiplexer #(.width(32)) multiplexer_2 (.in0(PROGRAM_COUNTER), .in1(rs1_data), .out(multiplexer_2_out), .sel(ASel));
  // Probe on multiplexer_2_out
  // Probe on ASel
  // Probe on multiplexer_3_out
  Multiplexer #(.width(32)) multiplexer_3 (.in0(imm), .in1(WRITE_DATA), .out(multiplexer_3_out), .sel(BSel));
  // Probe on WBSel
  // Probe on MemRW
  alu alu_1 (
    .Result(WRITE_ADDRESS), .A(multiplexer_2_out), .B(multiplexer_3_out), .ALUSel(ALUSel));  // open: out_5, out_6
  // Probe on WRITE_ADDRESS
  assign bit_extender_1_out = {{27{1'b0}}, INSTRUCTION[19:15]};  // Bit_Extender bit_extender_1
  Multiplexer #(.width(32)) multiplexer_4 (.in0(bit_extender_1_out), .in1(rs1_data), .out(CSR_din), .sel(CSRSel));
  Multiplexer #(.select(2), .width(32)) multiplexer_5 (
    .in0(READ_DATA), .in1(WRITE_ADDRESS), .in2(pcplus4), .out(WB), .sel(WBSel));  // open: in3
  csr csr_1 (.CSR_address(12'h51e), .CSR_din(CSR_din), .CSR_WE(CSRWen), .clk(clk), .tohost(tohost));
  assign WRITE_ENABLE = {{3{MemRW}}, MemRW};  // Bit_Extender bit_extender_2

  // Other names for the same wires on the sheet: aluresult[31:0] = WRITE_ADDRESS; rd[4:0] = INSTRUCTION[11:7];
  //   rs1[4:0] = INSTRUCTION[19:15]; imm_20_31[11:0] = INSTRUCTION[31:20]; rs2[4:0] = INSTRUCTION[24:20];
  //   funct7[6:0] = INSTRUCTION[31:25]; immed[6:0] = INSTRUCTION[31:25]; rs2_data[31:0] = WRITE_DATA

  // Notes on the sheet:
  //   PCSel
  //   Output to IMEM
  //   IMEM (do **NOT** move this)
  //   Inputs from IMEM
  //   It is OK to move the PC, RegFile, ALU, MEM, Branch Comp, Imm Gen, and Control Logic to wherever is most convenient for you when constructing your CPU, and to delete this text
  //   Inputs/Outputs for testing. Do **NOT** move these.
  //   Outputs To DMEM
  //   DMEM (do **NOT** move this)
  //   Inputs From DMEM
  //   MemRW only emit 1bit, but as we know, the WRITE_ENABLE have 4bits, each bit corresponds to overwritten status of  one byte
  //   that means , when MemRW equals to 1, the WRITE_ENABLE equals to 0b1111, that's to say, the WRITE_ADDRESS will writes to DMEM all bytes. 
  //   when MemRW equals to 0, the WRITE_ENABLE equals to 0b0000, that's to say, the WRITE_ADDRESS will writes to DMEM all zero. that is read
  //   why the aluresult is going to write to WRITE_ADDRESS: for example `ld x1, offset(x2)`, this inst would calculate the address of addition of offset and x2, then this result emitted from alu is a address of mem, used to indexing the mem data 
endmodule
