// Logisim project imm-gen.circ as structural Verilog: 1 circuit, main circuit imm_gen
module imm_gen (
  input  [31:0] inst,
  input  [2:0] ImmSel,
  output [31:0] imm
);

  wire [11:0] multiplexer_1_out;

  Multiplexer #(.enable("false"), .select(2), .width(12)) multiplexer_1 (
    .in0(inst[31:20]), .in1({inst[31:25], inst[11:7]}), .in3({inst[31], inst[7], inst[30:25], inst[11:8]}),
    .out(multiplexer_1_out), .sel(inst[6:5]));  // open: in2
  // Probe on {inst[31], inst[7], inst[30:25], inst[11:8]}
  // Probe on inst[6:5]
  // Probe on {inst[31:25], inst[11:7]}
  // Probe on inst[31:20]
  assign imm = {{20{multiplexer_1_out[11]}}, multiplexer_1_out};  // Bit_Extender bit_extender_1

  // Notes on the sheet:
  //   INPUTS to your circuit
  //   this probe only for debug, view the value within lines. either the 5th and 6th bit can decide how the imm generated or ImmSel needed
  //   DON'T CHANGE THE LOCATIONS OF THE INPUTS AND OUTPUTS!
  //   OUTPUT from your circuit
endmodule
