// Logisim project regfile.circ as structural Verilog: 1 circuit, main circuit regfile
module regfile (
  input  [4:0] rs1,
  input  [4:0] rs2,
  input  [4:0] rd,
  input  [31:0] Write_Data,
  input  RegWEn,
  input  clk,
  output [31:0] ra,
  output [31:0] sp,
  output [31:0] t0,
  output [31:0] t1,
  output [31:0] t2,
  output [31:0] s0,
  output [31:0] s1,
  output [31:0] a0,
  output [31:0] Read_Data_1,
  output [31:0] Read_Data_2
);

  wire a0_we, a1_we, a2_we, a3_we, a4_we, a5_we, a6_we, a7_we, gp_we, ra_we, s0_we, s1_we, s2_we, s3_we,
       s4_we, s5_we, s6_we, s7_we, s8_we, s9_we, s10_we, s11_we, sp_we, t0_we, t1_we, t2_we, t3_we, t4_we,
       t5_we, t6_we, tp_we, x0_we;
  wire [31:0] ra_out;

  Demultiplexer #(.enable("false"), .select(5)) demultiplexer_1 (
    .out0(ra_we), .out1(sp_we), .out2(gp_we), .out3(tp_we), .out4(t0_we), .out5(t1_we), .out6(t2_we),
    .out7(s0_we), .out8(s1_we), .out9(a0_we), .out10(a1_we), .out11(a2_we), .out12(a3_we), .out13(a4_we),
    .out14(a5_we), .out15(a6_we), .out16(a7_we), .out17(s2_we), .out18(s3_we), .out19(s4_we), .out20(s5_we),
    .out21(s6_we), .out22(s7_we), .out23(s8_we), .out24(s9_we), .out25(s10_we), .out26(s11_we),
    .out27(t3_we), .out28(t4_we), .out29(t5_we), .out30(t6_we), .out31(x0_we), .in(RegWEn), .sel(rd));
  Register #(.width(32)) register_1 (.D(Write_Data), .en(ra_we), .clk(clk), .Q(ra_out));  // open: clr

  // Other names for the same wires on the sheet: read_data1[31:0] = Read_Data_1; read_data2[31:0] = Read_Data_2;
  //   read_reg1[4:0] = rs1; read_reg2[4:0] = rs2; write_en = RegWEn; write_reg[4:0] = rd

  // Notes on the sheet:
  //   write enable signal
  //   INPUTS to your circuit
  //   DON'T CHANGE THE LOCATIONS OF THE INPUTS AND OUTPUTS!
  //   These are DEBUG/TEST outputs from your circuit.
  //   OUTPUTS from your circuit
endmodule
